// Logisim project Proiect.circ as structural Verilog: 13 circuits, main circuit CPU
module NAND (
  input  in_1,
  input  in_2,
  output out_3
);

  wire transistor_4_out;

  Transistor transistor_1 (.in(1'b1), .out(out_3), .gate(in_1));
  Transistor transistor_2 (.in(1'b1), .out(out_3), .gate(in_2));
  Transistor #(.\type ("n")) transistor_3 (.in(transistor_4_out), .out(out_3), .gate(in_1));
  Transistor #(.\type ("n")) transistor_4 (.in(1'b0), .out(transistor_4_out), .gate(in_2));
endmodule

module NOT_with_PMOS_NMOS (
  input  in_1,
  output out_2
);

  Transistor transistor_1 (.in(1'b1), .out(out_2), .gate(in_1));
  Transistor #(.\type ("n")) transistor_2 (.in(1'b0), .out(out_2), .gate(in_1));
endmodule

module NOT_NAND (
  input  in_1,
  output out_2
);

  NAND nand_1 (.in_1(in_1), .in_2(in_1), .out_3(out_2));
endmodule

module _1_bit_Register (
  input  i,
  input  S,
  output out_3
);

  wire nand_1_out, nand_2_out, nand_4_out, not_1_out;

  not not_1 (not_1_out, i);
  nand nand_1 (nand_1_out, i, S);
  nand nand_2 (nand_2_out, S, not_1_out);
  nand nand_3 (out_3, nand_1_out, nand_4_out);
  nand nand_4 (nand_4_out, out_3, nand_2_out);
endmodule

module _8_bit_Register__with_my_1_bit (
  input  S,
  input  in_2,
  input  in_3,
  input  in_4,
  input  in_5,
  input  in_6,
  input  in_7,
  input  in_8,
  input  in_9,
  output out_10,
  output out_11,
  output out_12,
  output out_13,
  output out_14,
  output out_15,
  output out_16,
  output out_17
);

  _1_bit_Register _1_bit_Register (.i(in_2), .S(S), .out_3(out_10));
  _1_bit_Register _1_bit_Register_2 (.i(in_3), .S(S), .out_3(out_11));
  _1_bit_Register _1_bit_Register_3 (.i(in_4), .S(S), .out_3(out_12));
  _1_bit_Register _1_bit_Register_4 (.i(in_5), .S(S), .out_3(out_13));
  _1_bit_Register _1_bit_Register_5 (.i(in_6), .S(S), .out_3(out_14));
  _1_bit_Register _1_bit_Register_6 (.i(in_7), .S(S), .out_3(out_15));
  _1_bit_Register _1_bit_Register_7 (.i(in_8), .S(S), .out_3(out_16));
  _1_bit_Register _1_bit_Register_8 (.i(in_9), .S(S), .out_3(out_17));
endmodule

module _8_bit_Register (
  input  CLK,
  input  EN,
  input  [7:0] IN,
  output [7:0] \reg 
);

  D_Flip_Flop d_ff_1 (.clk(CLK), .D(IN[0]), .Q(\reg [0]), .en(EN));  // open: Qn, preset, reset
  D_Flip_Flop d_ff_2 (.clk(CLK), .D(IN[1]), .Q(\reg [1]), .en(EN));  // open: Qn, preset, reset
  D_Flip_Flop d_ff_3 (.clk(CLK), .D(IN[2]), .Q(\reg [2]), .en(EN));  // open: Qn, preset, reset
  D_Flip_Flop d_ff_4 (.clk(CLK), .D(IN[3]), .Q(\reg [3]), .en(EN));  // open: Qn, preset, reset
  D_Flip_Flop d_ff_5 (.clk(CLK), .D(IN[4]), .Q(\reg [4]), .en(EN));  // open: Qn, preset, reset
  D_Flip_Flop d_ff_6 (.clk(CLK), .D(IN[5]), .Q(\reg [5]), .en(EN));  // open: Qn, preset, reset
  D_Flip_Flop d_ff_7 (.clk(CLK), .D(IN[6]), .Q(\reg [6]), .en(EN));  // open: Qn, preset, reset
  D_Flip_Flop d_ff_8 (.clk(CLK), .D(IN[7]), .Q(\reg [7]), .en(EN));  // open: Qn, preset, reset

  // Other names for the same wires on the sheet: a0 = IN[0]; a1 = IN[1]; a2 = IN[2]; a3 = IN[3]; a4 = IN[4];
  //   a5 = IN[5]; a6 = IN[6]; a7 = IN[7]
endmodule

module _2x4_Decoder (
  input  in_1,
  input  in_2,
  output out_3,
  output out_4,
  output out_5,
  output out_6
);

  wire nbit1, nbit2;

  not not_1 (nbit1, in_1);
  not not_2 (nbit2, in_2);
  and and_1 (out_3, nbit1, nbit2);
  and and_2 (out_4, in_1, nbit2);
  and and_3 (out_5, nbit1, in_2);
  and and_4 (out_6, in_1, in_2);

  // Other names for the same wires on the sheet: bit1 = in_1; bit2 = in_2
endmodule

module _2_1_MUX (
  input  in_1,
  input  in_2,
  input  in_3,
  output out_4
);

  wire nand_1_out, nand_2_out, not_1_out;

  not not_1 (not_1_out, in_3);
  nand nand_1 (nand_1_out, in_2, in_3);
  nand nand_2 (nand_2_out, not_1_out, in_1);
  nand nand_3 (out_4, nand_1_out, nand_2_out);

  // Other names for the same wires on the sheet: a = in_1; b = in_2; sel = in_3
endmodule

module XOR (
  input  in_1,
  input  in_2,
  output out_3
);

  wire nand_1_out_3, nand_2_out_3, nand_3_out_3, nand_4_out_3;

  NAND nand_1 (.in_1(in_1), .in_2(in_1), .out_3(nand_1_out_3));
  NAND nand_2 (.in_1(in_2), .in_2(in_2), .out_3(nand_2_out_3));
  NAND nand_3 (.in_1(in_1), .in_2(nand_2_out_3), .out_3(nand_3_out_3));
  NAND nand_4 (.in_1(nand_1_out_3), .in_2(in_2), .out_3(nand_4_out_3));
  NAND nand_5 (.in_1(nand_3_out_3), .in_2(nand_4_out_3), .out_3(out_3));
endmodule

module _1_bit_Adder (
  input  a,
  input  b,
  input  Cin,
  output S,
  output Cout
);

  wire nand_1_out, nand_2_out, not_1_out, not_2_out, xor_1_out;

  xor xor_1 (xor_1_out, a, b);
  nand nand_1 (nand_1_out, Cin, xor_1_out);
  nand nand_2 (nand_2_out, a, b);
  xor xor_2 (S, xor_1_out, Cin);
  not not_1 (not_1_out, nand_1_out);
  not not_2 (not_2_out, nand_2_out);
  xor xor_3 (Cout, not_1_out, not_2_out);
endmodule

module _8_bit_Adder (
  input  [7:0] a,
  input  [7:0] b,
  output [7:0] c,
  output cout
);

  wire n1_bit_adder_1_cout, n1_bit_adder_2_cout, n1_bit_adder_3_cout, n1_bit_adder_4_cout,
       n1_bit_adder_5_cout, n1_bit_adder_6_cout, n1_bit_adder_7_cout;

  _1_bit_Adder u_1_bit_adder_1 (.a(a[0]), .b(b[0]), .Cin(1'b0), .S(c[0]), .Cout(n1_bit_adder_1_cout));
  _1_bit_Adder u_1_bit_adder_2 (.a(a[1]), .b(b[1]), .Cin(n1_bit_adder_1_cout), .S(c[1]), .Cout(n1_bit_adder_2_cout));
  _1_bit_Adder u_1_bit_adder_3 (.a(a[2]), .b(b[2]), .Cin(n1_bit_adder_2_cout), .S(c[2]), .Cout(n1_bit_adder_3_cout));
  _1_bit_Adder u_1_bit_adder_4 (.a(a[3]), .b(b[3]), .Cin(n1_bit_adder_3_cout), .S(c[3]), .Cout(n1_bit_adder_4_cout));
  _1_bit_Adder u_1_bit_adder_5 (.a(a[4]), .b(b[4]), .Cin(n1_bit_adder_4_cout), .S(c[4]), .Cout(n1_bit_adder_5_cout));
  _1_bit_Adder u_1_bit_adder_6 (.a(a[5]), .b(b[5]), .Cin(n1_bit_adder_5_cout), .S(c[5]), .Cout(n1_bit_adder_6_cout));
  _1_bit_Adder u_1_bit_adder_7 (.a(a[6]), .b(b[6]), .Cin(n1_bit_adder_6_cout), .S(c[6]), .Cout(n1_bit_adder_7_cout));
  _1_bit_Adder u_1_bit_adder_8 (.a(a[7]), .b(b[7]), .Cin(n1_bit_adder_7_cout), .S(c[7]), .Cout(cout));
endmodule

module ALU (
  input  [7:0] a,
  input  [7:0] b,
  input  cin,
  output [7:0] c,
  output cout
);

  wire n8_bit_adder_2_cout, not_1_out;
  wire [7:0] multiplexer_1_out, n8_bit_adder_1_c, xor_1_out;

  assign xor_1_out = b ^ {8{cin}};  // XOR_Gate xor_1, 8 bits wide
  _8_bit_Adder u_8_bit_adder_1 (.a(xor_1_out), .b(8'h1), .c(n8_bit_adder_1_c));  // open: cout
  Multiplexer #(.width(8)) multiplexer_1 (
    .in0(b), .in1(n8_bit_adder_1_c), .out(multiplexer_1_out), .sel(cin), .en(1'b1));
  _8_bit_Adder u_8_bit_adder_2 (.a(a), .b(multiplexer_1_out), .c(c), .cout(n8_bit_adder_2_cout));
  Multiplexer multiplexer_2 (.in0(n8_bit_adder_2_cout), .in1(not_1_out), .out(cout), .sel(cin), .en(1'b1));
  not not_1 (not_1_out, n8_bit_adder_2_cout);
endmodule

module CPU (
  input  [7:0] keyboard,
  output [7:0] display
);

  wire A, ALU_cout, B, BUS0, BUS1, BUS2, C, CBIT, CLC, CLK, COUNT, FLAGS, IN, IR, LD, LDCOUNT, MAR,
       not_1_out, OPC0, OPC1, OPC2, OUT, STR, X;
  wire [2:0] SC_q;
  wire [3:0] INSTR_CODE, IR_q;
  wire [7:0] ALU1, ALU2, ALU_OUT, C_q, IN_q, MAR_q, multiplexer_1_out, PC_q, ram_1_data;

  Clock clock_1 (.out(CLK));
  Register u_MAR (.D(multiplexer_1_out), .en(MAR), .Q(MAR_q), .clk(CLK));  // open: clr
  Counter PC (.load(LDCOUNT), .D(multiplexer_1_out), .count(COUNT), .Q(PC_q), .clk(CLK));  // open: carry, clr
  Register u_A (.D(multiplexer_1_out), .en(A), .Q(ALU1), .clk(CLK));  // open: clr
  Register u_B (.D(multiplexer_1_out), .en(B), .Q(ALU2), .clk(CLK));  // open: clr
  Register u_C (.D(multiplexer_1_out), .en(C), .Q(C_q), .clk(CLK));  // open: clr
  Register u_IN (.D(keyboard), .en(IN), .Q(IN_q), .clk(CLK));  // open: clr
  Register u_OUT (.D(multiplexer_1_out), .en(OUT), .Q(display), .clk(CLK));  // open: clr
  Register u_IR (.D(multiplexer_1_out), .en(IR), .Q({INSTR_CODE, IR_q}), .clk(CLK));  // open: clr
  RAM #(.addrWidth(4), .bus("separate")) ram_1 (
    .addr(MAR_q[3:0]), .din(multiplexer_1_out), .data(ram_1_data), .str(STR), .sel(1'b1), .clk(CLK), .ld(LD),
    .clr(1'b0));
  Multiplexer #(.select(3), .width(8), .enable("false")) multiplexer_1 (
    .in0(ram_1_data), .in1(PC_q), .in2(ALU1), .in3(ALU2), .in4(C_q), .in5(IN_q), .in6(ALU_OUT),
    .in7({4'b0000, IR_q}), .out(multiplexer_1_out), .sel({BUS2, BUS1, BUS0}));
  Counter #(.width(3), .max('h7)) SC (.Q(SC_q), .clk(not_1_out), .clr(CLC));  // open: load, D, count, carry
  not not_1 (not_1_out, CLK);
  ALU ALU (.a(ALU1), .b(ALU2), .cin(OPC1), .c(ALU_OUT), .cout(ALU_cout));
  ROM #(.dataWidth(20)) rom_1 (
    .addr({CBIT, SC_q, INSTR_CODE}),
    .data({STR, LD, BUS2, BUS1, BUS0, MAR, COUNT, LDCOUNT, A, B, C, IN, OUT, IR, FLAGS, OPC2, OPC1, OPC0, CLC, X}),
    .sel(1'b1));
  Register #(.width(1)) u_FLAGS (.en(FLAGS), .Q(CBIT), .clk(CLK));  // open: D, clr

  // Notes on the sheet:
  //   CPU + Memory
  //   Microcode
  //   Arithmetic
  //   contents of rom_1 (hex, n*v repeats v):
  //   16*c000 16*42040 2 3c000 38800 10400 10200 18800 20800 10080 1c000 14000 30220 30228 39000 2 0 0 0
  //   40800 6*2 a0000 b8000 4*2 0 0 0 2 6*0 2 2 54*0 16*c000 16*42040 2 3c000 38800 10400 10200 18800
  //   20800 10080 1c000 14000 30220 30228 39000 39000 4*0 6*2 a0000 b8000 4*2 0 0 0 2 6*0 2 2 7*0 40800
endmodule
